// Logisim project alu.circ as structural Verilog: 1 circuit, main circuit main
module main (
  input  [31:0] X,
  input  [31:0] Y,
  input  [3:0] Switch,
  output Signed_Overflow,
  output Equal,
  output [31:0] Result,
  output [31:0] Result_2
);

  wire and_2_out, and_3_out, comparator_2_lt, comparator_3_lt, xnor_1_out, xor_1_out, xor_2_out, xor_3_out;
  wire [4:0] bit_extender_1_out, bit_extender_2_out, bit_extender_3_out;
  wire [31:0] adder_1_out, adder_2_out, adder_3_out, and_1_out, bit_extender_4_out, bit_extender_5_out,
       divider_1_out, divider_2_rem, multiplier_1_out, multiplier_2_cout, or_1_out, shifter_1_out,
       shifter_2_out, shifter_3_out, subtractor_1_out, subtractor_2_out, subtractor_3_out;

  Comparator #(.width(32)) comparator_1 (.a(X), .b(Y), .eq(Equal));  // open: gt, lt
  Bit_Extender #(.in_width(32), .out_width(5)) bit_extender_1 (.in(Y), .out(bit_extender_1_out));
  Bit_Extender #(.in_width(32), .out_width(5)) bit_extender_2 (.in(Y), .out(bit_extender_2_out));
  Bit_Extender #(.in_width(32), .out_width(5)) bit_extender_3 (.in(Y), .out(bit_extender_3_out));
  Shifter #(.width(32)) shifter_1 (.in(X), .\dist (bit_extender_1_out), .out(shifter_1_out));
  Shifter #(.width(32), .shift("lr")) shifter_2 (.in(X), .\dist (bit_extender_2_out), .out(shifter_2_out));
  Shifter #(.width(32), .shift("ar")) shifter_3 (.in(X), .\dist (bit_extender_3_out), .out(shifter_3_out));
  Multiplier #(.width(32)) multiplier_1 (.a(X), .b(Y), .out(multiplier_1_out));  // open: cin, cout
  Divider #(.width(32)) divider_1 (.a(X), .b(Y), .out(divider_1_out));  // open: upper, rem
  Adder #(.width(32)) adder_1 (.a(X), .b(Y), .out(adder_1_out));  // open: cin, cout
  Adder #(.width(32)) adder_2 (.a(X), .b(Y), .out(adder_2_out));  // open: cin, cout
  Subtractor #(.width(32)) subtractor_1 (.a(X), .b(Y), .out(subtractor_1_out));  // open: bin, bout
  Subtractor #(.width(32)) subtractor_2 (.a(X), .b(Y), .out(subtractor_2_out));  // open: bin, bout
  assign and_1_out = X & Y;  // AND_Gate and_1, 32 bits wide
  assign or_1_out = X | Y;  // OR_Gate or_1, 32 bits wide
  Comparator #(.width(32)) comparator_2 (.a(X), .b(Y), .lt(comparator_2_lt));  // open: gt, eq
  Comparator #(.width(32), .mode("unsigned")) comparator_3 (.a(X), .b(Y), .lt(comparator_3_lt));  // open: gt, eq
  assign bit_extender_4_out = {{31{1'b0}}, comparator_2_lt};  // Bit_Extender bit_extender_4
  assign bit_extender_5_out = {{31{1'b0}}, comparator_3_lt};  // Bit_Extender bit_extender_5
  Multiplexer #(.select(4), .width(32)) multiplexer_1 (
    .in0(shifter_1_out), .in1(shifter_2_out), .in2(shifter_3_out), .in3(multiplier_1_out),
    .in4(divider_1_out), .in5(adder_1_out), .in6(adder_2_out), .in7(subtractor_1_out),
    .in8(subtractor_2_out), .in9(and_1_out), .in10(or_1_out), .in11(bit_extender_4_out),
    .in12(bit_extender_5_out), .in13({32{1'b0}}), .in14({32{1'b0}}), .in15({32{1'b0}}), .out(Result),
    .sel(Switch));  // open: en
  xnor xnor_1 (xnor_1_out, X[31], Y[31]);
  Adder #(.width(32)) adder_3 (.a(X), .b(Y), .out(adder_3_out));  // open: cin, cout
  xor xor_1 (xor_1_out, X[31], Y[31]);
  Subtractor #(.width(32)) subtractor_3 (.a(X), .b(Y), .out(subtractor_3_out));  // open: bin, bout
  Multiplier #(.width(32)) multiplier_2 (.a(X), .b(Y), .cout(multiplier_2_cout));  // open: out, cin
  Divider #(.width(32)) divider_2 (.a(X), .b(Y), .rem(divider_2_rem));  // open: out, upper
  Multiplexer #(.select(4), .width(32)) multiplexer_2 (
    .in0({32{1'b0}}), .in1({32{1'b0}}), .in2({32{1'b0}}), .in3(multiplier_2_cout), .in4(divider_2_rem),
    .in5({32{1'b0}}), .in6({32{1'b0}}), .in7({32{1'b0}}), .in8({32{1'b0}}), .in9({32{1'b0}}),
    .in10({32{1'b0}}), .in11({32{1'b0}}), .in12({32{1'b0}}), .in13({32{1'b0}}), .in14({32{1'b0}}),
    .in15({32{1'b0}}), .out(Result_2), .sel(Switch));  // open: en
  and and_2 (and_2_out, xnor_1_out, xor_2_out);
  xor xor_2 (xor_2_out, X[31], adder_3_out[31]);
  and and_3 (and_3_out, xor_1_out, xor_3_out);
  xor xor_3 (xor_3_out, X[31], subtractor_3_out[31]);
  Multiplexer #(.select(4)) multiplexer_3 (
    .in0(1'b0), .in1(1'b0), .in2(1'b0), .in3(1'b0), .in4(1'b0), .in5(and_2_out), .in6(1'b0), .in7(and_3_out),
    .in8(1'b0), .in9(1'b0), .in10(1'b0), .in11(1'b0), .in12(1'b0), .in13(1'b0), .in14(1'b0), .in15(1'b0),
    .out(Signed_Overflow), .sel(Switch));  // open: en

  // Other names for the same wires on the sheet: overflow = Signed_Overflow; S[3:0] = Switch

  // Notes on the sheet:
  //   INPUTS to your circuit
  //   DON'T CHANGE THE LOCATIONS OF THE INPUTS AND OUTPUTS!
  //   OUTPUTS from your circuit
endmodule
