// Logisim project cpu.circ as structural Verilog: 2 circuits, main circuit main
module main (
  input  [31:0] INSTRUCTION,
  input  CLOCK,
  output [31:0] FETCH_ADDRESS,
  output [31:0] s0_Value,
  output [31:0] s1_Value,
  output [31:0] s2_Value,
  output [31:0] ra_Value,
  output [31:0] HI_Value,
  output [31:0] LO_Value
);

  wire ALUSrc, and_1_out, and_2_out, and_3_out, and_4_out, beqal, Bne, Equal, ExtOp, hi_t, j_jal_or_jr, Jump,
       lo_t, Lui, main_2_signed_overflow, MemtoReg, MemWrite, Mult_Div, multiplexer_3_out,
       multiplexer_21_out, not_1_out, not_2_out, nPCSel, RegDst, RegWrite, ReturnAdr, shamt_t, Swinc;
  wire [2:0] OpUnit;
  wire [3:0] ALUctr;
  wire [4:0] multiplexer_5_out, multiplexer_6_out, multiplexer_7_out;
  wire [5:0] funct;
  wire [15:0] bit_extender_1_out;
  wire [25:0] address;
  wire [31:0] adder_1_out, adder_2_out, ALU_R, ALU_R2, bit_extender_2_out, bit_extender_3_out, Data, imm,
       main_3_p6, multiplexer_1_out, multiplexer_4_out, multiplexer_8_out, multiplexer_9_out,
       multiplexer_10_out, multiplexer_11_out, multiplexer_12_out, multiplexer_13_out, multiplexer_14_out,
       multiplexer_15_out, multiplexer_16_out, multiplexer_17_out, multiplexer_18_out, multiplexer_20_out,
       multiplexer_22_out, multiplexer_24_out, multiplexer_25_out, PC_4, RegR1, RegR2, shifter_1_out, To_PC;
  wire [31:6] inst;

  Multiplexer #(.width(32)) multiplexer_1 (
    .in0(INSTRUCTION), .in1({32{1'b0}}), .out(multiplexer_1_out), .sel(Jump));  // open: en
  assign bit_extender_1_out = {{11{1'b0}}, inst[10:6]};  // Bit_Extender bit_extender_1
  and and_1 (and_1_out, nPCSel, Equal);
  Multiplexer #(.width(16)) multiplexer_2 (
    .in0({inst[15:6], funct}), .in1(bit_extender_1_out), .out(address[15:0]), .sel(shamt_t));  // open: en
  not not_1 (not_1_out, Equal);
  and and_2 (and_2_out, Bne, not_1_out);
  Multiplexer multiplexer_3 (.in0(and_1_out), .in1(and_2_out), .out(multiplexer_3_out), .sel(Bne));  // open: en
  Multiplexer #(.width(32)) multiplexer_4 (
    .in0(multiplexer_1_out), .in1({32{1'b0}}), .out(multiplexer_4_out), .sel(multiplexer_3_out));  // open: en
  Multiplexer #(.width(5), .enable("false")) multiplexer_5 (
    .in0(address[20:16]), .in1(inst[15:11]), .out(multiplexer_5_out), .sel(RegDst));
  Register #(.width(32)) register_1 (
    .D(multiplexer_4_out), .Q({inst[31:26], address[25:16], inst[15:6], funct}), .clk(CLOCK));  // open: en, clr
  Multiplexer #(.width(5), .enable("false")) multiplexer_6 (
    .in0(multiplexer_5_out), .in1({5{1'b1}}), .out(multiplexer_6_out), .sel(ReturnAdr));
  Multiplexer #(.width(5)) multiplexer_7 (
    .in0(multiplexer_6_out), .in1(address[25:21]), .out(multiplexer_7_out), .sel(Swinc));  // open: en
  Multiplexer #(.width(32)) multiplexer_8 (
    .in0(multiplexer_9_out), .in1(adder_1_out), .out(multiplexer_8_out), .sel(Swinc));  // open: en
  Multiplexer #(.width(32)) multiplexer_9 (
    .in0(multiplexer_10_out), .in1(multiplexer_11_out), .out(multiplexer_9_out), .sel(beqal));  // open: en
  Multiplexer #(.width(32)) multiplexer_10 (
    .in0(multiplexer_12_out), .in1(HI_Value), .out(multiplexer_10_out), .sel(hi_t));  // open: en
  Multiplexer #(.width(32)) multiplexer_11 (
    .in1(FETCH_ADDRESS), .out(multiplexer_11_out), .sel(Equal));  // open: in0, en
  Multiplexer #(.width(32)) multiplexer_12 (
    .in0(multiplexer_13_out), .in1(LO_Value), .out(multiplexer_12_out), .sel(lo_t));  // open: en
  Multiplexer #(.width(32), .enable("false")) multiplexer_13 (
    .in0(Data), .in1(FETCH_ADDRESS), .out(multiplexer_13_out), .sel(ReturnAdr));
  regfile_main main_1 (
    .Read_Register_1(address[25:21]), .Read_Register_2(address[20:16]), .Write_Register(multiplexer_7_out),
    .Write_Data(multiplexer_8_out), .Write_Enable(RegWrite), .Clock(CLOCK), .Read_Data_1(RegR1),
    .Read_Data_2(RegR2), .s0_Value(s0_Value), .s1_Value(s1_Value), .s2_Value(s2_Value), .ra_Value(ra_Value));
  Control control_1 (
    .Opcode(inst[31:26]), .Funct(funct), .RegDst(RegDst), .Mult_Div(Mult_Div), .ALUSrc(ALUSrc),
    .nPCsel(nPCSel), .J_Jal_or_Jr(j_jal_or_jr), .Jump(Jump), .MemtoReg(MemtoReg), .ALUctr(ALUctr),
    .MemWrite(MemWrite), .hi(hi_t), .beqal(beqal), .ReturnAdr(ReturnAdr), .lo(lo_t), .OpUnit(OpUnit),
    .shamt(shamt_t), .RegWrite(RegWrite), .Bne(Bne), .Swinc(Swinc), .Lui(Lui), .ExtOp(ExtOp));
  Multiplexer #(.width(32), .enable("false")) multiplexer_14 (
    .in0(RegR2), .in1(imm), .out(multiplexer_14_out), .sel(ALUSrc));
  Adder #(.width(32)) adder_1 (.a(RegR1), .b(imm), .out(adder_1_out));  // open: cin, cout
  Multiplexer #(.width(32)) multiplexer_15 (.in0(RegR1), .in1(imm), .out(multiplexer_15_out), .sel(Lui));  // open: en
  Multiplexer #(.width(32)) multiplexer_16 (
    .in0(multiplexer_15_out), .in1(RegR2), .out(multiplexer_16_out), .sel(shamt_t));  // open: en
  Multiplexer #(.width(32)) multiplexer_17 (
    .in0(multiplexer_14_out), .in1(imm), .out(multiplexer_17_out), .sel(shamt_t));  // open: en
  LED Overflow (.in(main_2_signed_overflow));
  alu_main main_2 (
    .Switch(ALUctr), .X(multiplexer_16_out), .Equal(Equal), .Result(ALU_R),
    .Signed_Overflow(main_2_signed_overflow), .Y(multiplexer_18_out), .Result_2(ALU_R2));
  Multiplexer #(.width(32)) multiplexer_18 (
    .in0(multiplexer_17_out), .in1(32'h10), .out(multiplexer_18_out), .sel(Lui));  // open: en
  assign bit_extender_2_out = {{16{1'b0}}, address[15:0]};  // Bit_Extender bit_extender_2
  assign bit_extender_3_out = {{16{address[15]}}, address[15:0]};  // Bit_Extender bit_extender_3
  Multiplexer #(.width(32), .enable("false")) multiplexer_19 (
    .in0(bit_extender_2_out), .in1(bit_extender_3_out), .out(imm), .sel(ExtOp));
  Multiplexer #(.width(32), .enable("false")) multiplexer_20 (
    .in1(ALU_R), .out(multiplexer_20_out), .sel(Mult_Div));  // open: in0
  Shifter #(.width(32)) shifter_1 (.in(imm), .\dist (5'b00010), .out(shifter_1_out));
  Register #(.width(32)) LO (.D(multiplexer_20_out), .Q(LO_Value));  // open: en, clk, clr
  and and_3 (and_3_out, nPCSel, Equal);
  Adder #(.width(32)) adder_2 (.a(FETCH_ADDRESS), .b(shifter_1_out), .out(adder_2_out));  // open: cin, cout
  // mem_main main_3: pin names not known; wires that end beside it: ALU_R, RegR2, MemWrite, CLOCK, OpUnit, main_3_p6
  Register #(.width(32)) PC (.D(To_PC), .Q(FETCH_ADDRESS), .clk(CLOCK));  // open: en, clr
  and and_4 (and_4_out, Bne, not_2_out);
  Multiplexer multiplexer_21 (.in0(and_3_out), .in1(and_4_out), .out(multiplexer_21_out), .sel(Bne));  // open: en
  Multiplexer #(.width(32), .enable("false")) multiplexer_22 (
    .in0(PC_4), .in1(adder_2_out), .out(multiplexer_22_out), .sel(multiplexer_21_out));
  Multiplexer #(.width(32), .enable("false")) multiplexer_23 (.in0(ALU_R), .in1(main_3_p6), .out(Data), .sel(MemtoReg));
  Register #(.width(32)) HI (.D(multiplexer_24_out), .Q(HI_Value));  // open: en, clk, clr
  Multiplexer #(.width(32), .enable("false")) multiplexer_24 (
    .in1(ALU_R2), .out(multiplexer_24_out), .sel(Mult_Div));  // open: in0
  not not_2 (not_2_out, Equal);
  Adder #(.width(32)) adder_3 (.a(FETCH_ADDRESS), .b(32'h4), .out(PC_4));  // open: cin, cout
  Multiplexer #(.width(32), .enable("false")) multiplexer_25 (
    .in0({FETCH_ADDRESS[31:28], address, 2'b00}), .in1(RegR1), .out(multiplexer_25_out), .sel(j_jal_or_jr));
  Multiplexer #(.width(32), .enable("false")) multiplexer_26 (
    .in0(multiplexer_22_out), .in1(multiplexer_25_out), .out(To_PC), .sel(Jump));

  // Other names for the same wires on the sheet: inst (some bits) = {address[25:16], funct}; shamt[4:0] = inst[10:6];
  //   rd[4:0] = inst[15:11]; immediate[15:0] = address[15:0]; rt[4:0] = address[20:16]; rs[4:0] = address[25:21];
  //   fetch_addr[31:0] = FETCH_ADDRESS; PC[31:0] = FETCH_ADDRESS; clk = CLOCK; HI[31:0] = HI_Value;
  //   opcode[5:0] = inst[31:26]; LO[31:0] = LO_Value; ra[31:0] = ra_Value; s0[31:0] = s0_Value; s1[31:0] = s1_Value;
  //   s2[31:0] = s2_Value

  // Notes on the sheet:
  //   Extract Pieces from Instruction
  //   Output
  //   These are outputs/inputs from run.circ
  //   Inputs
  //   These are DEBUG/TEST outputs from your circuit.
  //   Sign/Zero Extend Immediate
  //   MULTU/DIVU Instructions
  //   PC Logic
endmodule

module Control (
  input  [5:0] Opcode,
  input  [5:0] Funct,
  output [3:0] ALUctr,
  output RegDst,
  output J_Jal_or_Jr,
  output Jump,
  output MemWrite,
  output nPCsel,
  output Mult_Div,
  output MemtoReg,
  output hi,
  output beqal,
  output ReturnAdr,
  output ALUSrc,
  output lo,
  output [2:0] OpUnit,
  output shamt,
  output RegWrite,
  output Bne,
  output Swinc,
  output Lui,
  output ExtOp
);

  wire and_5_out, and_7_out, and_8_out, and_9_out, and_10_out, and_11_out, and_12_out, and_13_out,
       and_14_out, and_15_out, and_16_out, and_18_out, and_19_out, and_20_out, and_21_out, and_24_out,
       and_25_out, and_26_out, and_27_out, and_28_out, and_29_out, and_30_out, and_31_out, and_32_out,
       and_33_out, and_34_out, and_35_out, and_36_out, comparator_1_eq, comparator_3_eq, comparator_4_eq,
       comparator_5_eq, comparator_6_eq, comparator_7_eq, comparator_8_eq, comparator_9_eq, comparator_10_eq,
       comparator_11_eq, comparator_13_eq, comparator_14_eq, comparator_15_eq, comparator_16_eq,
       comparator_17_eq, comparator_18_eq, comparator_19_eq, comparator_20_eq, comparator_21_eq,
       comparator_22_eq, comparator_23_eq, comparator_24_eq, comparator_25_eq, comparator_26_eq,
       comparator_27_eq, comparator_28_eq, comparator_29_eq, comparator_30_eq, comparator_31_eq,
       comparator_32_eq, comparator_33_eq, comparator_34_eq, comparator_35_eq, comparator_36_eq,
       comparator_37_eq, comparator_39_eq, comparator_40_eq, comparator_42_eq, comparator_43_eq,
       comparator_44_eq, comparator_45_eq, comparator_46_eq, comparator_47_eq, comparator_48_eq,
       comparator_49_eq, comparator_50_eq, comparator_51_eq, comparator_52_eq, comparator_53_eq,
       comparator_54_eq, comparator_55_eq, comparator_56_eq, comparator_57_eq, comparator_58_eq,
       comparator_59_eq, comparator_60_eq, comparator_61_eq, comparator_62_eq, comparator_63_eq,
       comparator_64_eq, comparator_65_eq, comparator_66_eq, comparator_67_eq, comparator_68_eq, not_1_out,
       not_2_out, not_3_out, not_4_out, not_5_out, not_6_out, not_7_out, not_8_out, not_9_out, not_10_out,
       not_11_out, not_12_out, not_13_out, not_14_out, not_15_out, not_16_out, not_17_out, not_18_out,
       not_19_out, not_20_out, not_21_out, not_22_out, not_23_out, or_1_out, or_2_out, or_6_out, or_7_out,
       or_8_out, or_9_out, or_11_out, or_12_out, or_13_out, or_14_out, or_15_out, or_16_out;

  not not_1 (not_1_out, Opcode[3]);
  not not_2 (not_2_out, Opcode[4]);
  not not_3 (not_3_out, Opcode[5]);
  and and_1 (RegDst, not_3_out, not_2_out, not_1_out, not_5_out, not_6_out, not_4_out);
  Comparator #(.width(6)) comparator_1 (.a(Funct), .b(6'b011011), .eq(comparator_1_eq));  // open: gt, lt
  or or_1 (or_1_out, comparator_1_eq, comparator_3_eq);
  and and_2 (Mult_Div, RegDst, or_1_out);
  Comparator #(.width(6)) comparator_2 (.a(Opcode), .b(6'b010100), .eq(beqal));  // open: gt, lt
  not not_4 (not_4_out, Opcode[0]);
  not not_5 (not_5_out, Opcode[2]);
  not not_6 (not_6_out, Opcode[1]);
  Comparator #(.width(6)) comparator_3 (.a(Funct), .b(6'b011001), .eq(comparator_3_eq));  // open: gt, lt
  Comparator #(.width(6)) comparator_4 (.a(Opcode), .b(6'b100000), .eq(comparator_4_eq));  // open: gt, lt
  Comparator #(.width(6)) comparator_5 (.a(Opcode), .b(6'b100100), .eq(comparator_5_eq));  // open: gt, lt
  Comparator #(.width(6)) comparator_6 (.a(Opcode), .b(6'b100101), .eq(comparator_6_eq));  // open: gt, lt
  Comparator #(.width(6)) comparator_7 (.a(Opcode), .b(6'b100011), .eq(comparator_7_eq));  // open: gt, lt
  Comparator #(.width(6)) comparator_8 (.a(Opcode), .b(6'b101000), .eq(comparator_8_eq));  // open: gt, lt
  Comparator #(.width(6)) comparator_9 (.a(Opcode), .b(6'b101001), .eq(comparator_9_eq));  // open: gt, lt
  Comparator #(.width(6)) comparator_10 (.a(Opcode), .b(6'b101011), .eq(comparator_10_eq));  // open: gt, lt
  Comparator #(.width(6)) comparator_11 (.a(Opcode), .b(6'b101100), .eq(comparator_11_eq));  // open: gt, lt
  not not_7 (not_7_out, Opcode[4]);
  not not_8 (not_8_out, Opcode[5]);
  not not_9 (not_9_out, Opcode[3]);
  not not_10 (not_10_out, Opcode[1]);
  and and_3 (nPCsel, not_8_out, not_9_out, Opcode[2], not_10_out, or_2_out);
  not not_11 (not_11_out, nPCsel);
  not not_12 (not_12_out, RegDst);
  and and_4 (ALUSrc, not_12_out, not_11_out);
  Multiplexer #(.width(3)) multiplexer_1 (.in1(3'b001), .out(OpUnit), .sel(comparator_4_eq));  // open: in0, en
  Multiplexer #(.width(3)) multiplexer_2 (.in1(3'b000), .out(OpUnit), .sel(comparator_5_eq));  // open: in0, en
  Multiplexer #(.width(3)) multiplexer_3 (.in1(3'b010), .out(OpUnit), .sel(comparator_6_eq));  // open: in0, en
  Multiplexer #(.width(3)) multiplexer_4 (.in1(3'b100), .out(OpUnit), .sel(comparator_7_eq));  // open: in0, en
  Multiplexer #(.width(3)) multiplexer_5 (.in1(3'b001), .out(OpUnit), .sel(comparator_8_eq));  // open: in0, en
  Multiplexer #(.width(3)) multiplexer_6 (.in1(3'b011), .out(OpUnit), .sel(comparator_9_eq));  // open: in0, en
  Multiplexer #(.width(3)) multiplexer_7 (.in1(3'b100), .out(OpUnit), .sel(comparator_10_eq));  // open: in0, en
  Multiplexer #(.width(3)) multiplexer_8 (.in1(3'b100), .out(OpUnit), .sel(comparator_11_eq));  // open: in0, en
  Comparator #(.width(6)) comparator_12 (.a(Opcode), .b(6'b101100), .eq(Swinc));  // open: gt, lt
  not not_13 (not_13_out, Opcode[0]);
  and and_5 (and_5_out, Opcode[4], not_13_out);
  or or_2 (or_2_out, not_7_out, and_5_out);
  Comparator #(.width(6), .mode("unsigned")) comparator_13 (
    .a(Opcode), .b(6'b101000), .eq(comparator_13_eq));  // open: gt, lt
  Comparator #(.width(6), .mode("unsigned")) comparator_14 (
    .a(Opcode), .b(6'b101001), .eq(comparator_14_eq));  // open: gt, lt
  Comparator #(.width(6), .mode("unsigned")) comparator_15 (
    .a(Opcode), .b(6'b101011), .eq(comparator_15_eq));  // open: gt, lt
  Comparator #(.width(6), .mode("unsigned")) comparator_16 (
    .a(Opcode), .b(6'b101100), .eq(comparator_16_eq));  // open: gt, lt
  Comparator #(.width(6)) comparator_17 (.a(Funct), .b(6'b011011), .eq(comparator_17_eq));  // open: gt, lt
  Comparator #(.width(6)) comparator_18 (.a(Funct), .b(6'b001000), .eq(comparator_18_eq));  // open: gt, lt
  Comparator #(.width(6)) comparator_19 (.a(Funct), .b(6'b011001), .eq(comparator_19_eq));  // open: gt, lt
  Comparator #(.width(6)) comparator_20 (.a(Funct), .b({6{1'b0}}), .eq(comparator_20_eq));  // open: gt, lt
  Comparator #(.width(6)) comparator_21 (.a(Funct), .b(6'b000011), .eq(comparator_21_eq));  // open: gt, lt
  Comparator #(.width(6)) comparator_22 (.a(Funct), .b(6'b000010), .eq(comparator_22_eq));  // open: gt, lt
  Comparator #(.width(6)) comparator_23 (.a(Funct), .b(6'b001000), .eq(comparator_23_eq));  // open: gt, lt
  and and_6 (J_Jal_or_Jr, comparator_23_eq, RegDst);
  or or_3 (Jump, J_Jal_or_Jr, and_10_out);
  or or_4 (MemWrite, comparator_13_eq, comparator_14_eq, comparator_15_eq, comparator_16_eq);
  Comparator #(.width(6), .mode("unsigned")) comparator_24 (
    .a(Opcode), .b(6'b000011), .eq(comparator_24_eq));  // open: gt, lt
  Comparator #(.width(6), .mode("unsigned")) comparator_25 (
    .a(Opcode), .b(6'b010100), .eq(comparator_25_eq));  // open: gt, lt
  Comparator #(.width(6)) comparator_26 (.a(Opcode), .b(6'b000100), .eq(comparator_26_eq));  // open: gt, lt
  Comparator #(.width(6)) comparator_27 (.a(Opcode), .b(6'b000101), .eq(comparator_27_eq));  // open: gt, lt
  Comparator #(.width(6)) comparator_28 (.a(Opcode), .b(6'b000010), .eq(comparator_28_eq));  // open: gt, lt
  Comparator #(.width(6)) comparator_29 (.a(Opcode), .b(6'b101000), .eq(comparator_29_eq));  // open: gt, lt
  Comparator #(.width(6)) comparator_30 (.a(Opcode), .b(6'b101001), .eq(comparator_30_eq));  // open: gt, lt
  Comparator #(.width(6)) comparator_31 (.a(Opcode), .b(6'b101011), .eq(comparator_31_eq));  // open: gt, lt
  Comparator #(.width(6)) comparator_32 (.a(Opcode), .b(6'b001100), .eq(comparator_32_eq));  // open: gt, lt
  Comparator #(.width(6)) comparator_33 (.a(Opcode), .b(6'b001111), .eq(comparator_33_eq));  // open: gt, lt
  Comparator #(.width(6)) comparator_34 (.a(Opcode), .b(6'b001101), .eq(comparator_34_eq));  // open: gt, lt
  and and_7 (and_7_out, comparator_20_eq, RegDst);
  and and_8 (and_8_out, comparator_21_eq, RegDst);
  and and_9 (and_9_out, comparator_22_eq, RegDst);
  not not_14 (not_14_out, Opcode[3]);
  not not_15 (not_15_out, Opcode[2]);
  not not_16 (not_16_out, Opcode[5]);
  not not_17 (not_17_out, Opcode[4]);
  and and_10 (and_10_out, not_16_out, not_17_out, not_14_out, not_15_out, Opcode[1]);
  not not_18 (not_18_out, Opcode[0]);
  not not_19 (not_19_out, Opcode[1]);
  and and_11 (and_11_out, not_19_out, not_18_out);
  or or_5 (ReturnAdr, comparator_24_eq, comparator_25_eq);
  and and_12 (and_12_out, comparator_17_eq, RegDst);
  and and_13 (and_13_out, comparator_18_eq, RegDst);
  and and_14 (and_14_out, comparator_19_eq, RegDst);
  not not_20 (not_20_out, Opcode[2]);
  and and_15 (and_15_out, not_20_out, Opcode[1]);
  or or_6 (or_6_out, and_15_out, and_18_out);
  and and_16 (and_16_out, Opcode[0], or_6_out);
  or or_7 (or_7_out, and_11_out, and_16_out);
  and and_17 (MemtoReg, or_7_out, Opcode[5], not_22_out, not_23_out);
  or or_8 (or_8_out, comparator_32_eq, comparator_33_eq, comparator_34_eq, and_7_out, and_8_out, and_9_out);
  not not_21 (not_21_out, Opcode[1]);
  and and_18 (and_18_out, Opcode[2], not_21_out);
  not not_22 (not_22_out, Opcode[4]);
  not not_23 (not_23_out, Opcode[3]);
  Comparator #(.width(6)) comparator_35 (.a(Funct), .b({6{1'b0}}), .eq(comparator_35_eq));  // open: gt, lt
  Comparator #(.width(6)) comparator_36 (.a(Funct), .b(6'b000011), .eq(comparator_36_eq));  // open: gt, lt
  Comparator #(.width(6)) comparator_37 (.a(Funct), .b(6'b000010), .eq(comparator_37_eq));  // open: gt, lt
  or or_9 (or_9_out, comparator_26_eq, comparator_27_eq, and_12_out, comparator_28_eq, and_13_out, and_14_out, comparator_29_eq, comparator_30_eq, comparator_31_eq);
  not not_24 (RegWrite, or_9_out);
  Comparator #(.width(6)) comparator_38 (.a(Opcode), .b(6'b001111), .eq(Lui));  // open: gt, lt
  not not_25 (ExtOp, or_8_out);
  Comparator #(.width(6), .mode("unsigned")) comparator_39 (
    .a(Funct), .b(6'b010000), .eq(comparator_39_eq));  // open: gt, lt
  Comparator #(.width(6), .mode("unsigned")) comparator_40 (
    .a(Funct), .b(6'b010010), .eq(comparator_40_eq));  // open: gt, lt
  and and_19 (and_19_out, comparator_35_eq, RegDst);
  and and_20 (and_20_out, comparator_36_eq, RegDst);
  and and_21 (and_21_out, comparator_37_eq, RegDst);
  Comparator #(.width(6)) comparator_41 (.a(Opcode), .b(6'b000101), .eq(Bne));  // open: gt, lt
  and and_22 (hi, comparator_39_eq, RegDst);
  and and_23 (lo, RegDst, comparator_40_eq);
  or or_10 (shamt, and_19_out, and_20_out, and_21_out);
  Comparator #(.width(6)) comparator_42 (.a(Funct), .b(6'b100000), .eq(comparator_42_eq));  // open: gt, lt
  Comparator #(.width(6)) comparator_43 (.a(Opcode), .b(6'b001000), .eq(comparator_43_eq));  // open: gt, lt
  Comparator #(.width(6)) comparator_44 (.a(Opcode), .b(6'b100000), .eq(comparator_44_eq));  // open: gt, lt
  Comparator #(.width(6)) comparator_45 (.a(Opcode), .b(6'b100011), .eq(comparator_45_eq));  // open: gt, lt
  Comparator #(.width(6)) comparator_46 (.a(Opcode), .b(6'b101000), .eq(comparator_46_eq));  // open: gt, lt
  Comparator #(.width(6)) comparator_47 (.a(Opcode), .b(6'b101001), .eq(comparator_47_eq));  // open: gt, lt
  Comparator #(.width(6)) comparator_48 (.a(Opcode), .b(6'b101011), .eq(comparator_48_eq));  // open: gt, lt
  Comparator #(.width(6)) comparator_49 (.a(Opcode), .b(6'b101100), .eq(comparator_49_eq));  // open: gt, lt
  Comparator #(.width(6)) comparator_50 (.a(Opcode), .b(6'b001001), .eq(comparator_50_eq));  // open: gt, lt
  Comparator #(.width(6)) comparator_51 (.a(Funct), .b(6'b100001), .eq(comparator_51_eq));  // open: gt, lt
  Comparator #(.width(6)) comparator_52 (.a(Opcode), .b(6'b100100), .eq(comparator_52_eq));  // open: gt, lt
  Comparator #(.width(6)) comparator_53 (.a(Opcode), .b(6'b100101), .eq(comparator_53_eq));  // open: gt, lt
  Comparator #(.width(6)) comparator_54 (.a(Funct), .b(6'b100100), .eq(comparator_54_eq));  // open: gt, lt
  Comparator #(.width(6)) comparator_55 (.a(Opcode), .b(6'b001100), .eq(comparator_55_eq));  // open: gt, lt
  Comparator #(.width(6)) comparator_56 (.a(Funct), .b(6'b011011), .eq(comparator_56_eq));  // open: gt, lt
  Comparator #(.width(6)) comparator_57 (.a(Funct), .b(6'b011001), .eq(comparator_57_eq));  // open: gt, lt
  Comparator #(.width(6)) comparator_58 (.a(Opcode), .b(6'b001111), .eq(comparator_58_eq));  // open: gt, lt
  Comparator #(.width(6)) comparator_59 (.a(Funct), .b({6{1'b0}}), .eq(comparator_59_eq));  // open: gt, lt
  Comparator #(.width(6)) comparator_60 (.a(Opcode), .b(6'b001101), .eq(comparator_60_eq));  // open: gt, lt
  Comparator #(.width(6)) comparator_61 (.a(Funct), .b(6'b100101), .eq(comparator_61_eq));  // open: gt, lt
  Comparator #(.width(6)) comparator_62 (.a(Opcode), .b(6'b001010), .eq(comparator_62_eq));  // open: gt, lt
  Comparator #(.width(6)) comparator_63 (.a(Funct), .b(6'b101010), .eq(comparator_63_eq));  // open: gt, lt
  Comparator #(.width(6)) comparator_64 (.a(Funct), .b(6'b101011), .eq(comparator_64_eq));  // open: gt, lt
  Comparator #(.width(6)) comparator_65 (.a(Funct), .b(6'b000011), .eq(comparator_65_eq));  // open: gt, lt
  Comparator #(.width(6)) comparator_66 (.a(Funct), .b(6'b000010), .eq(comparator_66_eq));  // open: gt, lt
  Comparator #(.width(6)) comparator_67 (.a(Funct), .b(6'b100010), .eq(comparator_67_eq));  // open: gt, lt
  Comparator #(.width(6)) comparator_68 (.a(Funct), .b(6'b100011), .eq(comparator_68_eq));  // open: gt, lt
  and and_24 (and_24_out, comparator_42_eq, RegDst);
  and and_25 (and_25_out, comparator_51_eq, RegDst);
  and and_26 (and_26_out, comparator_54_eq, RegDst);
  and and_27 (and_27_out, comparator_56_eq, RegDst);
  and and_28 (and_28_out, comparator_57_eq, RegDst);
  and and_29 (and_29_out, comparator_59_eq, RegDst);
  and and_30 (and_30_out, comparator_61_eq, RegDst);
  and and_31 (and_31_out, comparator_63_eq, RegDst);
  and and_32 (and_32_out, comparator_64_eq, RegDst);
  and and_33 (and_33_out, comparator_65_eq, RegDst);
  and and_34 (and_34_out, comparator_66_eq, RegDst);
  and and_35 (and_35_out, comparator_67_eq, RegDst);
  and and_36 (and_36_out, comparator_68_eq, RegDst);
  or or_11 (or_11_out, comparator_50_eq, and_25_out, comparator_52_eq, comparator_53_eq);
  Multiplexer #(.width(4)) multiplexer_9 (.in1(4'b1001), .out(ALUctr), .sel(or_12_out));  // open: in0, en
  or or_12 (or_12_out, and_26_out, comparator_55_eq);
  Multiplexer #(.width(4)) multiplexer_10 (.in1(4'b0100), .out(ALUctr), .sel(and_27_out));  // open: in0, en
  Multiplexer #(.width(4)) multiplexer_11 (.in1(4'b0011), .out(ALUctr), .sel(and_28_out));  // open: in0, en
  or or_13 (or_13_out, comparator_58_eq, and_29_out);
  or or_14 (or_14_out, comparator_60_eq, and_30_out);
  or or_15 (or_15_out, comparator_62_eq, and_31_out);
  Multiplexer #(.width(4)) multiplexer_12 (.in1(4'b1100), .out(ALUctr), .sel(and_32_out));  // open: in0, en
  Multiplexer #(.width(4)) multiplexer_13 (.in1(4'b0010), .out(ALUctr), .sel(and_33_out));  // open: in0, en
  Multiplexer #(.width(4)) multiplexer_14 (.in1(4'b0001), .out(ALUctr), .sel(and_34_out));  // open: in0, en
  Multiplexer #(.width(4)) multiplexer_15 (.in1(4'b0111), .out(ALUctr), .sel(and_35_out));  // open: in0, en
  Multiplexer #(.width(4)) multiplexer_16 (.in1(4'b1000), .out(ALUctr), .sel(and_36_out));  // open: in0, en
  Multiplexer #(.width(4)) multiplexer_17 (.in1(4'b0110), .out(ALUctr), .sel(or_11_out));  // open: in0, en
  Multiplexer #(.width(4)) multiplexer_18 (.in1(4'b0000), .out(ALUctr), .sel(or_13_out));  // open: in0, en
  Multiplexer #(.width(4)) multiplexer_19 (.in1(4'b1010), .out(ALUctr), .sel(or_14_out));  // open: in0, en
  Multiplexer #(.width(4)) multiplexer_20 (.in1(4'b1011), .out(ALUctr), .sel(or_15_out));  // open: in0, en
  Multiplexer #(.width(4)) multiplexer_21 (.in1(4'b0101), .out(ALUctr), .sel(or_16_out));  // open: in0, en
  or or_16 (or_16_out, and_24_out, comparator_43_eq, comparator_44_eq, comparator_45_eq, comparator_46_eq, comparator_47_eq, comparator_48_eq, comparator_49_eq);

  // Other names for the same wires on the sheet: R_type = RegDst
endmodule
