// Logisim project regfile.circ as structural Verilog: 1 circuit, main circuit main
module main (
  input  [4:0] Read_Register_1,
  input  [4:0] Read_Register_2,
  input  [4:0] Write_Register,
  input  [31:0] Write_Data,
  input  Write_Enable,
  input  Clock,
  output [31:0] s0_Value,
  output [31:0] s1_Value,
  output [31:0] s2_Value,
  output [31:0] ra_Value,
  output [31:0] Read_Data_1,
  output [31:0] Read_Data_2
);

  wire and_1_out, W1, W2, W3, W4, W5, W6, W7, W8, W9, W10, W11, W12, W13, W14, W15, W16, W17, W18, W19, W20,
       W21, W22, W23, W24, W25, W26, W27, W28, W29, W30, W31, W32;
  wire [31:0] _1, _2, _3, _4, _5, _6, _7, _8, _9, _10, _11, _12, _13, _14, _15, _16, _20, _21, _22, _23, _24,
       _25, _26, _27, _28, _29, _30, _31, R1, R2, R3, R4, R5, R6, R7, R8, R9, R10, R11, R12, R13, R14, R15,
       R16, R17, R18, R19, R20, R21, R22, R23, R24, R25, R26, R27, R28, R29, R30, R31, R32;

  Multiplexer #(.width(32)) multiplexer_1 (.in0(_12), .in1(Write_Data), .out(R12), .sel(W12));  // open: en
  Multiplexer #(.width(32)) multiplexer_2 (.in0(_11), .in1(Write_Data), .out(R11), .sel(W11));  // open: en
  Multiplexer #(.width(32)) multiplexer_3 (.in0(_10), .in1(Write_Data), .out(R10), .sel(W10));  // open: en
  Multiplexer #(.width(32)) multiplexer_4 (.in0(_9), .in1(Write_Data), .out(R9), .sel(W9));  // open: en
  Register #(.width(32)) register_1 (.D(R12), .Q(_12), .clk(Clock));  // open: en, clr
  Register #(.width(32)) register_2 (.D(R11), .Q(_11), .clk(Clock));  // open: en, clr
  Register #(.width(32)) register_3 (.D(R10), .Q(_10), .clk(Clock));  // open: en, clr
  Register #(.width(32)) register_4 (.D(R9), .Q(_9), .clk(Clock));  // open: en, clr
  Demultiplexer #(.select(5)) demultiplexer_1 (
    .out0(W1), .out1(W2), .out2(W3), .out3(W4), .out4(W5), .out5(W6), .out6(W7), .out7(W8), .out8(W9),
    .out9(W10), .out10(W11), .out11(W12), .out12(W13), .out13(W14), .out14(W15), .out15(W16), .out16(W17),
    .out17(W18), .out18(W19), .out19(W20), .out20(W21), .out21(W22), .out22(W23), .out23(W24), .out24(W25),
    .out25(W26), .out26(W27), .out27(W28), .out28(W29), .out29(W30), .out30(W31), .out31(W32),
    .in(and_1_out), .sel(Write_Register));  // open: en
  and and_1 (and_1_out, Write_Enable, 1'b1);
  Multiplexer #(.width(32)) multiplexer_5 (.in0(_1), .in1({32{1'b0}}), .out(R1), .sel(W1));  // open: en
  Multiplexer #(.width(32)) multiplexer_6 (.in0(_2), .in1(Write_Data), .out(R2), .sel(W2));  // open: en
  Multiplexer #(.width(32)) multiplexer_7 (.in0(_3), .in1(Write_Data), .out(R3), .sel(W3));  // open: en
  Multiplexer #(.width(32)) multiplexer_8 (.in0(_4), .in1(Write_Data), .out(R4), .sel(W4));  // open: en
  Multiplexer #(.width(32)) multiplexer_9 (.in0(_16), .in1(Write_Data), .out(R16), .sel(W16));  // open: en
  Multiplexer #(.width(32)) multiplexer_10 (.in0(_15), .in1(Write_Data), .out(R15), .sel(W15));  // open: en
  Multiplexer #(.width(32)) multiplexer_11 (.in0(_14), .in1(Write_Data), .out(R14), .sel(W14));  // open: en
  Multiplexer #(.width(32)) multiplexer_12 (.in0(_13), .in1(Write_Data), .out(R13), .sel(W13));  // open: en
  Register #(.width(32)) register_5 (.D(R1), .Q(_1), .clk(Clock));  // open: en, clr
  Register #(.width(32)) register_6 (.D(R2), .Q(_2), .clk(Clock));  // open: en, clr
  Register #(.width(32)) register_7 (.D(R3), .Q(_3), .clk(Clock));  // open: en, clr
  Register #(.width(32)) register_8 (.D(R4), .Q(_4), .clk(Clock));  // open: en, clr
  Register #(.width(32)) register_9 (.D(R16), .Q(_16), .clk(Clock));  // open: en, clr
  Register #(.width(32)) register_10 (.D(R15), .Q(_15), .clk(Clock));  // open: en, clr
  Register #(.width(32)) register_11 (.D(R14), .Q(_14), .clk(Clock));  // open: en, clr
  Register #(.width(32)) register_12 (.D(R13), .Q(_13), .clk(Clock));  // open: en, clr
  Multiplexer #(.width(32)) multiplexer_13 (.in0(_5), .in1(Write_Data), .out(R5), .sel(W5));  // open: en
  Multiplexer #(.width(32)) multiplexer_14 (.in0(_6), .in1(Write_Data), .out(R6), .sel(W6));  // open: en
  Multiplexer #(.width(32)) multiplexer_15 (.in0(_7), .in1(Write_Data), .out(R7), .sel(W7));  // open: en
  Multiplexer #(.width(32)) multiplexer_16 (.in0(_8), .in1(Write_Data), .out(R8), .sel(W8));  // open: en
  Multiplexer #(.width(32)) multiplexer_17 (.in0(_21), .in1(Write_Data), .out(R21), .sel(W21));  // open: en
  Multiplexer #(.width(32)) multiplexer_18 (.in0(_22), .in1(Write_Data), .out(R22), .sel(W22));  // open: en
  Multiplexer #(.width(32)) multiplexer_19 (.in0(_23), .in1(Write_Data), .out(R23), .sel(W23));  // open: en
  Multiplexer #(.width(32)) multiplexer_20 (.in0(_24), .in1(Write_Data), .out(R24), .sel(W24));  // open: en
  Multiplexer #(.width(32)) multiplexer_21 (.in0(s0_Value), .in1(Write_Data), .out(R17), .sel(W17));  // open: en
  Multiplexer #(.width(32)) multiplexer_22 (.in0(s1_Value), .in1(Write_Data), .out(R18), .sel(W18));  // open: en
  Multiplexer #(.width(32)) multiplexer_23 (.in0(s2_Value), .in1(Write_Data), .out(R19), .sel(W19));  // open: en
  Multiplexer #(.width(32)) multiplexer_24 (.in0(_20), .in1(Write_Data), .out(R20), .sel(W20));  // open: en
  Register #(.width(32)) register_13 (.D(R5), .Q(_5), .clk(Clock));  // open: en, clr
  Register #(.width(32)) register_14 (.D(R6), .Q(_6), .clk(Clock));  // open: en, clr
  Register #(.width(32)) register_15 (.D(R7), .Q(_7), .clk(Clock));  // open: en, clr
  Register #(.width(32)) register_16 (.D(R8), .Q(_8), .clk(Clock));  // open: en, clr
  Register #(.width(32)) register_17 (.D(R17), .Q(s0_Value), .clk(Clock));  // open: en, clr
  Register #(.width(32)) register_18 (.D(R18), .Q(s1_Value), .clk(Clock));  // open: en, clr
  Register #(.width(32)) register_19 (.D(R19), .Q(s2_Value), .clk(Clock));  // open: en, clr
  Register #(.width(32)) register_20 (.D(R20), .Q(_20), .clk(Clock));  // open: en, clr
  Register #(.width(32)) register_21 (.D(R21), .Q(_21), .clk(Clock));  // open: en, clr
  Register #(.width(32)) register_22 (.D(R22), .Q(_22), .clk(Clock));  // open: en, clr
  Register #(.width(32)) register_23 (.D(R23), .Q(_23), .clk(Clock));  // open: en, clr
  Register #(.width(32)) register_24 (.D(R24), .Q(_24), .clk(Clock));  // open: en, clr
  Multiplexer #(.width(32)) multiplexer_25 (.in0(_28), .in1(Write_Data), .out(R28), .sel(W28));  // open: en
  Multiplexer #(.width(32)) multiplexer_26 (.in0(_27), .in1(Write_Data), .out(R27), .sel(W27));  // open: en
  Multiplexer #(.width(32)) multiplexer_27 (.in0(_26), .in1(Write_Data), .out(R26), .sel(W26));  // open: en
  Multiplexer #(.width(32)) multiplexer_28 (.in0(_25), .in1(Write_Data), .out(R25), .sel(W25));  // open: en
  Multiplexer #(.select(5), .width(32), .enable("false")) multiplexer_29 (
    .in0(_1), .in1(_2), .in2(_3), .in3(_4), .in4(_5), .in5(_6), .in6(_7), .in7(_8), .in8(_9), .in9(_10),
    .in10(_11), .in11(_12), .in12(_13), .in13(_14), .in14(_15), .in15(_16), .in16(s0_Value), .in17(s1_Value),
    .in18(s2_Value), .in19(_20), .in20(_21), .in21(_22), .in22(_23), .in23(_24), .in24(_25), .in25(_26),
    .in26(_27), .in27(_28), .in28(_29), .in29(_30), .in30(_31), .in31(ra_Value), .out(Read_Data_1),
    .sel(Read_Register_1));
  Multiplexer #(.select(5), .width(32), .enable("false")) multiplexer_30 (
    .in0(_1), .in1(_2), .in2(_3), .in3(_4), .in4(_5), .in5(_6), .in6(_7), .in7(_8), .in8(_9), .in9(_10),
    .in10(_11), .in11(_12), .in12(_13), .in13(_14), .in14(_15), .in15(_16), .in16(s0_Value), .in17(s1_Value),
    .in18(s2_Value), .in19(_20), .in20(_21), .in21(_22), .in22(_23), .in23(_24), .in24(_25), .in25(_26),
    .in26(_27), .in27(_28), .in28(_29), .in29(_30), .in30(_31), .in31(ra_Value), .out(Read_Data_2),
    .sel(Read_Register_2));
  Register #(.width(32)) register_25 (.D(R28), .Q(_28), .clk(Clock));  // open: en, clr
  Register #(.width(32)) register_26 (.D(R27), .Q(_27), .clk(Clock));  // open: en, clr
  Register #(.width(32)) register_27 (.D(R26), .Q(_26), .clk(Clock));  // open: en, clr
  Register #(.width(32)) register_28 (.D(R25), .Q(_25), .clk(Clock));  // open: en, clr
  Multiplexer #(.width(32)) multiplexer_31 (.in0(_29), .in1(Write_Data), .out(R29), .sel(W29));  // open: en
  Multiplexer #(.width(32)) multiplexer_32 (.in0(_30), .in1(Write_Data), .out(R30), .sel(W30));  // open: en
  Multiplexer #(.width(32)) multiplexer_33 (.in0(_31), .in1(Write_Data), .out(R31), .sel(W31));  // open: en
  Multiplexer #(.width(32)) multiplexer_34 (.in0(ra_Value), .in1(Write_Data), .out(R32), .sel(W32));  // open: en
  Register #(.width(32)) register_29 (.D(R29), .Q(_29), .clk(Clock));  // open: en, clr
  Register #(.width(32)) register_30 (.D(R30), .Q(_30), .clk(Clock));  // open: en, clr
  Register #(.width(32)) register_31 (.D(R31), .Q(_31), .clk(Clock));  // open: en, clr
  Register #(.width(32)) register_32 (.D(R32), .Q(ra_Value), .clk(Clock));  // open: en, clr

  // Other names for the same wires on the sheet: _17[31:0] = s0_Value; _18[31:0] = s1_Value; _19[31:0] = s2_Value;
  //   _32[31:0] = ra_Value; clk = Clock; read_data1[31:0] = Read_Data_1; read_data2[31:0] = Read_Data_2;
  //   read_reg1[4:0] = Read_Register_1; read_reg2[4:0] = Read_Register_2; write_en = Write_Enable;
  //   write_reg[4:0] = Write_Register

  // Notes on the sheet:
  //   INPUTS to your circuit
  //   DON'T CHANGE THE LOCATIONS OF THE INPUTS AND OUTPUTS!
  //   These are DEBUG/TEST outputs from your circuit.
  //   OUTPUTS from your circuit
endmodule
